// Logisim project aiAlu.circ as structural Verilog
module aiArith (
  input  [7:0] A,
  input  [7:0] B
);

  wire [7:0] aisum_1_sum, aisum_2_sum, twocomplement_1_out;

  twoComplement twocomplement_1 (.In(B), .Out(twocomplement_1_out));
  aiSum aisum_1 (.Carry_In(1'b0), .A(A), .B(B), .Sum(aisum_1_sum));  // open: Carry_Out
  aiSum aisum_2 (.Carry_In(1'b0), .A(A), .B(twocomplement_1_out), .Sum(aisum_2_sum));  // open: Carry_Out

  // Notes on the sheet:
  //   A + B
  //   A - B
endmodule

module MUX_4_inputs (
  input  [1:0] Select,
  input  [3:0] Data,
  output Output
);

  wire and_1_out, and_2_out, and_3_out, and_4_out, not_1_out, not_2_out, not_3_out, not_4_out;

  and and_1 (and_1_out, Select[0], Select[1], Data[3]);
  not not_1 (not_1_out, Select[0]);
  and and_2 (and_2_out, not_1_out, Select[1], Data[2]);
  not not_2 (not_2_out, Select[1]);
  and and_3 (and_3_out, Select[0], not_2_out, Data[1]);
  not not_3 (not_3_out, Select[0]);
  not not_4 (not_4_out, Select[1]);
  and and_4 (and_4_out, not_3_out, not_4_out, Data[0]);
  or or_1 (Output, and_1_out, and_2_out, and_3_out, and_4_out);
endmodule

module fullAdder (
  input  A,
  input  B,
  input  Carry_In,
  output Output,
  output Carry_Out
);

  wire and_1_out, and_2_out, and_3_out, xor_1_out;

  xor xor_1 (xor_1_out, A, B);
  and and_1 (and_1_out, A, B);
  and and_2 (and_2_out, B, Carry_In);
  and and_3 (and_3_out, A, Carry_In);
  xor xor_2 (Output, xor_1_out, Carry_In);
  or or_1 (Carry_Out, and_1_out, and_2_out, and_3_out);
endmodule

module aiSum (
  input  Carry_In,
  input  [7:0] A,
  input  [7:0] B,
  output [7:0] Sum,
  output Carry_Out
);

  wire fulladder_1_carry_out, fulladder_2_carry_out, fulladder_3_carry_out, fulladder_4_carry_out,
       fulladder_5_carry_out, fulladder_6_carry_out, fulladder_7_carry_out;

  fullAdder fulladder_1 (.A(A[0]), .B(B[0]), .Carry_In(Carry_In), .Output(Sum[0]), .Carry_Out(fulladder_1_carry_out));
  fullAdder fulladder_2 (
    .A(A[1]), .B(B[1]), .Carry_In(fulladder_1_carry_out), .Output(Sum[1]), .Carry_Out(fulladder_2_carry_out));
  fullAdder fulladder_3 (
    .A(A[2]), .B(B[2]), .Carry_In(fulladder_2_carry_out), .Output(Sum[2]), .Carry_Out(fulladder_3_carry_out));
  fullAdder fulladder_4 (
    .A(A[3]), .B(B[3]), .Carry_In(fulladder_3_carry_out), .Output(Sum[3]), .Carry_Out(fulladder_4_carry_out));
  fullAdder fulladder_5 (
    .A(A[4]), .B(B[4]), .Carry_In(fulladder_4_carry_out), .Output(Sum[4]), .Carry_Out(fulladder_5_carry_out));
  fullAdder fulladder_6 (
    .A(A[5]), .B(B[5]), .Carry_In(fulladder_5_carry_out), .Output(Sum[5]), .Carry_Out(fulladder_6_carry_out));
  fullAdder fulladder_7 (
    .A(A[6]), .B(B[6]), .Carry_In(fulladder_6_carry_out), .Output(Sum[6]), .Carry_Out(fulladder_7_carry_out));
  fullAdder fulladder_8 (.A(A[7]), .B(B[7]), .Carry_In(fulladder_7_carry_out), .Output(Sum[7]), .Carry_Out(Carry_Out));
endmodule

module AND (
  input  [7:0] in_1,
  input  [7:0] in_2,
  output [7:0] out_3
);

  assign out_3 = in_1 & in_2;  // AND_Gate and_1, 8 bits wide
endmodule

module OR (
  input  [7:0] in_1,
  input  [7:0] in_2,
  output [7:0] out_3
);

  assign out_3 = in_1 | in_2;  // OR_Gate or_1, 8 bits wide
endmodule

module NOT_A (
  input  [7:0] in_1,
  output [7:0] out_2
);

  assign out_2 = ~in_1;  // NOT_Gate not_1, 8 bits wide
endmodule

module NOT_B (
  input  [7:0] in_1,
  output [7:0] out_2
);

  assign out_2 = ~in_1;  // NOT_Gate not_1, 8 bits wide
endmodule

module XOR (
  input  [7:0] in_1,
  input  [7:0] in_2,
  output [7:0] out_3
);

  assign out_3 = in_1 ^ in_2;  // XOR_Gate xor_1, 8 bits wide
endmodule

module twoComplement (
  input  [7:0] In,
  output [7:0] Out
);

  wire [7:0] not_1_out;

  not not_1 (not_1_out[0], In[0]);
  not not_2 (not_1_out[1], In[1]);
  not not_3 (not_1_out[2], In[2]);
  not not_4 (not_1_out[3], In[3]);
  not not_5 (not_1_out[4], In[4]);
  not not_6 (not_1_out[5], In[5]);
  not not_7 (not_1_out[6], In[6]);
  not not_8 (not_1_out[7], In[7]);
  aiSum aisum_1 (.Carry_In(1'b0), .A(not_1_out), .B(8'h1), .Sum(Out));  // open: Carry_Out
endmodule
